// Logisim project Computer.circ as structural Verilog: 9 circuits, main circuit main
module main (
  input  in_1,
  input  in_2,
  input  in_3,
  input  in_4
);

  wire clock_1_out, clock_2_out, controll_rom_1_out_5, controll_rom_1_out_7, controll_rom_1_out_8,
       controll_rom_1_out_9, controll_rom_1_out_11, flag_register_1_out_4, multiplexer_1_out, not_1_out;
  wire [1:0] controll_rom_1_out_13;
  wire [3:0] alu_1_out_5, controll_rom_1_out_6, controll_rom_1_out_10, controll_rom_1_out_12,
       controll_rom_1_out_16;
  wire [7:0] alu_1_out_6, controll_rom_1_out_15, instruction_memory_1_out_6, instruction_memory_1_out_7,
       instruction_memory_1_out_8, instruction_memory_1_out_9, multiplexer_2_out, multiplexer_3_out,
       register_file_1_out_6, register_file_1_out_7, rom_1_data;
  wire [13:0] controll_rom_1_out_14, program_counter_1_out_5;
  wire [15:0] counter_1_q;

  not not_1 (not_1_out, clock_1_out);
  Clock clock_1 (.out(clock_1_out));
  Multi_Bit_Bidirectional_Shift_Register multi_bit_bidirectional_shift_register_1 ();  // open: in_1, in_2, in_3, in_4, out_5, out_6
  Clock clock_2 (.out(clock_2_out));
  Counter #(.width(16), .max('hffff), .ongoal("stay")) counter_1 (
    .Q(counter_1_q), .clk(not_1_out), .clr(in_1));  // open: load, D, count, carry
  Multiplexer multiplexer_1 (
    .in0(controll_rom_1_out_8), .in1(flag_register_1_out_4), .out(multiplexer_1_out),
    .sel(controll_rom_1_out_11));  // open: en
  Program_Counter program_counter_1 (
    .in_1(controll_rom_1_out_14), .in_2(multiplexer_1_out), .in_3(clock_2_out), .in_4(in_3),
    .out_5(program_counter_1_out_5));
  ROM #(.addrWidth(16)) rom_1 (.addr(counter_1_q), .data(rom_1_data));  // open: sel
  Instruction_Memory instruction_memory_1 (
    .in_1(rom_1_data), .in_2(in_2), .out_6(instruction_memory_1_out_6), .in_4(program_counter_1_out_5),
    .in_5(clock_1_out), .out_7(instruction_memory_1_out_7), .out_8(instruction_memory_1_out_8),
    .out_9(instruction_memory_1_out_9), .in_3(counter_1_q));
  Controll_Rom controll_rom_1 (
    .in_1(instruction_memory_1_out_6), .out_5(controll_rom_1_out_5), .out_6(controll_rom_1_out_6),
    .in_2(instruction_memory_1_out_7), .in_3(instruction_memory_1_out_8), .in_4(instruction_memory_1_out_9),
    .out_10(controll_rom_1_out_10), .out_12(controll_rom_1_out_12), .out_16(controll_rom_1_out_16),
    .out_9(controll_rom_1_out_9), .out_15(controll_rom_1_out_15), .out_7(controll_rom_1_out_7),
    .out_14(controll_rom_1_out_14), .out_13(controll_rom_1_out_13), .out_8(controll_rom_1_out_8),
    .out_11(controll_rom_1_out_11));
  Multiplexer #(.width(8)) multiplexer_2 (
    .in0(alu_1_out_6), .in1(controll_rom_1_out_15), .out(multiplexer_2_out), .sel(controll_rom_1_out_9));  // open: en
  Register_File register_file_1 (
    .in_1(multiplexer_2_out), .in_4(controll_rom_1_out_10), .out_6(register_file_1_out_6),
    .in_5(controll_rom_1_out_12), .out_7(register_file_1_out_7), .in_2(controll_rom_1_out_16),
    .in_3(clock_2_out));
  Multiplexer #(.width(8)) multiplexer_3 (
    .in0(register_file_1_out_7), .in1(controll_rom_1_out_15), .out(multiplexer_3_out),
    .sel(controll_rom_1_out_7));  // open: en
  ALU alu_1 (
    .in_1(register_file_1_out_6), .in_2(multiplexer_3_out), .in_3(controll_rom_1_out_6),
    .in_4(controll_rom_1_out_5), .out_6(alu_1_out_6), .out_5(alu_1_out_5));
  Flag_Register flag_register_1 (
    .in_1(clock_2_out), .in_2(alu_1_out_5), .in_3(controll_rom_1_out_13), .out_4(flag_register_1_out_4));

  // Notes on the sheet:
  //   contents of rom_1 (hex, n*v repeats v):
  //   6 10 3 0 2 0 0 0 a 10 0 0 6 20 a 0 6 30 e 0 6 40 f
endmodule

module ALU (
  input  [7:0] in_1,
  input  [7:0] in_2,
  input  [3:0] in_3,
  input  in_4,
  output [3:0] out_5,
  output [7:0] out_6
);

  wire [7:0] adder_1_out, demultiplexer_1_out0, demultiplexer_1_out1, demultiplexer_1_out2,
       demultiplexer_1_out3, demultiplexer_2_out0, demultiplexer_2_out1, demultiplexer_2_out2,
       demultiplexer_2_out3, divider_1_out, multiplier_1_out, subtractor_1_out;

  Demultiplexer #(.select(4), .width(8)) demultiplexer_1 (
    .out0(demultiplexer_1_out0), .out1(demultiplexer_1_out1), .out2(demultiplexer_1_out2),
    .out3(demultiplexer_1_out3), .in(in_1), .sel(in_3), .en(in_4));  // open: out4, out5, out6, out7, out8, out9, out10, out11, out12, out13, out14, out15
  Demultiplexer #(.select(4), .width(8)) demultiplexer_2 (
    .out0(demultiplexer_2_out0), .out1(demultiplexer_2_out1), .out2(demultiplexer_2_out2),
    .out3(demultiplexer_2_out3), .in(in_2), .sel(in_3), .en(in_4));  // open: out4, out5, out6, out7, out8, out9, out10, out11, out12, out13, out14, out15
  Adder adder_1 (.a(demultiplexer_1_out0), .b(demultiplexer_2_out0), .out(adder_1_out), .cout(out_5[1]));  // open: cin
  Subtractor subtractor_1 (
    .a(demultiplexer_1_out1), .b(demultiplexer_2_out1), .out(subtractor_1_out));  // open: bin, bout
  Multiplier multiplier_1 (
    .a(demultiplexer_1_out2), .b(demultiplexer_2_out2), .out(multiplier_1_out));  // open: cin, cout
  Divider divider_1 (.a(demultiplexer_1_out3), .b(demultiplexer_2_out3), .out(divider_1_out));  // open: upper, rem
  Multiplexer #(.select(4), .width(8)) multiplexer_1 (
    .in0(adder_1_out), .in1(subtractor_1_out), .in2(multiplier_1_out), .in3(divider_1_out), .out(out_6),
    .sel(in_3), .en(in_4));  // open: in4, in5, in6, in7, in8, in9, in10, in11, in12, in13, in14, in15
  Comparator comparator_1 (.a({8{1'b0}}), .b(out_6), .eq(out_5[0]));  // open: gt, lt
endmodule

module Register_File (
  input  [7:0] in_1,
  input  [3:0] in_2,
  input  in_3,
  input  [3:0] in_4,
  input  [3:0] in_5,
  output [7:0] out_6,
  output [7:0] out_7
);

  wire decoder_1_out1, decoder_1_out2, decoder_1_out3, decoder_1_out4, decoder_1_out5, decoder_1_out6,
       decoder_1_out7, decoder_1_out8, decoder_1_out9, decoder_1_out10, decoder_1_out11, decoder_1_out12,
       decoder_1_out13, decoder_1_out14, decoder_1_out15;
  wire [7:0] controlled_buffer_1_out, controlled_buffer_2_out, controlled_buffer_3_out,
       controlled_buffer_4_out, controlled_buffer_5_out, controlled_buffer_6_out, controlled_buffer_7_out,
       controlled_buffer_8_out, controlled_buffer_9_out, controlled_buffer_10_out, controlled_buffer_11_out,
       controlled_buffer_12_out, controlled_buffer_13_out, controlled_buffer_14_out,
       controlled_buffer_15_out, register_1_q, register_2_q, register_3_q, register_4_q, register_5_q,
       register_6_q, register_7_q, register_8_q, register_9_q, register_10_q, register_11_q, register_12_q,
       register_13_q, register_14_q, register_15_q, register_16_q;

  Decoder #(.select(4)) decoder_1 (
    .out1(decoder_1_out1), .out2(decoder_1_out2), .out3(decoder_1_out3), .out4(decoder_1_out4),
    .out5(decoder_1_out5), .out6(decoder_1_out6), .out7(decoder_1_out7), .out8(decoder_1_out8),
    .out9(decoder_1_out9), .out10(decoder_1_out10), .out11(decoder_1_out11), .out12(decoder_1_out12),
    .out13(decoder_1_out13), .out14(decoder_1_out14), .out15(decoder_1_out15), .sel(in_2));  // open: out0, en
  Register register_1 (.Q(register_1_q));  // open: D, en, clk, clr
  Register register_2 (.D(controlled_buffer_1_out), .en(decoder_1_out1), .Q(register_2_q), .clk(in_3));  // open: clr
  assign controlled_buffer_1_out = decoder_1_out1 ? in_1 : 8'bz;  // Controlled_Buffer controlled_buffer_1
  assign controlled_buffer_2_out = decoder_1_out2 ? in_1 : 8'bz;  // Controlled_Buffer controlled_buffer_2
  Register register_3 (.D(controlled_buffer_2_out), .en(decoder_1_out2), .Q(register_3_q), .clk(in_3));  // open: clr
  assign controlled_buffer_3_out = decoder_1_out3 ? in_1 : 8'bz;  // Controlled_Buffer controlled_buffer_3
  Register register_4 (.D(controlled_buffer_3_out), .en(decoder_1_out3), .Q(register_4_q), .clk(in_3));  // open: clr
  assign controlled_buffer_4_out = decoder_1_out4 ? in_1 : 8'bz;  // Controlled_Buffer controlled_buffer_4
  Register register_5 (.D(controlled_buffer_4_out), .en(decoder_1_out4), .Q(register_5_q), .clk(in_3));  // open: clr
  Register register_6 (.D(controlled_buffer_5_out), .en(decoder_1_out5), .Q(register_6_q), .clk(in_3));  // open: clr
  assign controlled_buffer_5_out = decoder_1_out5 ? in_1 : 8'bz;  // Controlled_Buffer controlled_buffer_5
  Register register_7 (.D(controlled_buffer_6_out), .en(decoder_1_out6), .Q(register_7_q), .clk(in_3));  // open: clr
  assign controlled_buffer_6_out = decoder_1_out6 ? in_1 : 8'bz;  // Controlled_Buffer controlled_buffer_6
  Register register_8 (.D(controlled_buffer_7_out), .en(decoder_1_out7), .Q(register_8_q), .clk(in_3));  // open: clr
  assign controlled_buffer_7_out = decoder_1_out7 ? in_1 : 8'bz;  // Controlled_Buffer controlled_buffer_7
  assign controlled_buffer_8_out = decoder_1_out8 ? in_1 : 8'bz;  // Controlled_Buffer controlled_buffer_8
  Register register_9 (.D(controlled_buffer_8_out), .en(decoder_1_out8), .Q(register_9_q), .clk(in_3));  // open: clr
  Register register_10 (.D(controlled_buffer_9_out), .en(decoder_1_out9), .Q(register_10_q), .clk(in_3));  // open: clr
  assign controlled_buffer_9_out = decoder_1_out9 ? in_1 : 8'bz;  // Controlled_Buffer controlled_buffer_9
  assign controlled_buffer_10_out = decoder_1_out10 ? in_1 : 8'bz;  // Controlled_Buffer controlled_buffer_10
  Register register_11 (
    .D(controlled_buffer_10_out), .en(decoder_1_out10), .Q(register_11_q), .clk(in_3));  // open: clr
  Register register_12 (
    .D(controlled_buffer_11_out), .en(decoder_1_out11), .Q(register_12_q), .clk(in_3));  // open: clr
  assign controlled_buffer_11_out = decoder_1_out11 ? in_1 : 8'bz;  // Controlled_Buffer controlled_buffer_11
  assign controlled_buffer_12_out = decoder_1_out12 ? in_1 : 8'bz;  // Controlled_Buffer controlled_buffer_12
  Register register_13 (
    .D(controlled_buffer_12_out), .en(decoder_1_out12), .Q(register_13_q), .clk(in_3));  // open: clr
  Register register_14 (
    .D(controlled_buffer_13_out), .en(decoder_1_out13), .Q(register_14_q), .clk(in_3));  // open: clr
  assign controlled_buffer_13_out = decoder_1_out13 ? in_1 : 8'bz;  // Controlled_Buffer controlled_buffer_13
  assign controlled_buffer_14_out = decoder_1_out14 ? in_1 : 8'bz;  // Controlled_Buffer controlled_buffer_14
  Register register_15 (
    .D(controlled_buffer_14_out), .en(decoder_1_out14), .Q(register_15_q), .clk(in_3));  // open: clr
  assign controlled_buffer_15_out = decoder_1_out15 ? in_1 : 8'bz;  // Controlled_Buffer controlled_buffer_15
  Register register_16 (
    .D(controlled_buffer_15_out), .en(decoder_1_out15), .Q(register_16_q), .clk(in_3));  // open: clr
  Multiplexer #(.select(4), .width(8)) multiplexer_1 (
    .in0(register_1_q), .in1(register_2_q), .in2(register_3_q), .in3(register_4_q), .in4(register_5_q),
    .in5(register_6_q), .in6(register_7_q), .in7(register_8_q), .in8(register_9_q), .in9(register_10_q),
    .in10(register_11_q), .in11(register_12_q), .in12(register_13_q), .in13(register_14_q),
    .in14(register_15_q), .in15(register_16_q), .out(out_6), .sel(in_4));  // open: en
  Multiplexer #(.select(4), .width(8)) multiplexer_2 (
    .in0(register_1_q), .in1(register_2_q), .in2(register_3_q), .in3(register_4_q), .in4(register_5_q),
    .in5(register_6_q), .in6(register_7_q), .in7(register_8_q), .in8(register_9_q), .in9(register_10_q),
    .in10(register_11_q), .in11(register_12_q), .in12(register_13_q), .in13(register_14_q),
    .in14(register_15_q), .in15(register_16_q), .out(out_7), .sel(in_5));  // open: en
endmodule

module Instruction_Memory (
  input  [7:0] in_1,
  input  in_2,
  input  [15:0] in_3,
  input  [13:0] in_4,
  input  in_5,
  output [7:0] out_6,
  output [7:0] out_7,
  output [7:0] out_8,
  output [7:0] out_9
);

  wire not_1_out, not_2_out, not_3_out, not_4_out;
  wire [15:0] adder_1_out, adder_2_out, adder_3_out, bit_extender_1_out, multiplexer_1_out,
       multiplexer_2_out, multiplexer_3_out, multiplexer_4_out, multiplier_1_out, multiplier_2_out,
       multiplier_3_out, multiplier_4_out;

  assign bit_extender_1_out = {{2{1'b0}}, in_4};  // Bit_Extender bit_extender_1
  Multiplier #(.width(16)) multiplier_1 (.a(bit_extender_1_out), .b(16'h4), .out(multiplier_1_out));  // open: cin, cout
  Multiplier #(.width(16)) multiplier_2 (.a(bit_extender_1_out), .b(16'h4), .out(multiplier_2_out));  // open: cin, cout
  Multiplier #(.width(16)) multiplier_3 (.a(bit_extender_1_out), .b(16'h4), .out(multiplier_3_out));  // open: cin, cout
  Multiplier #(.width(16)) multiplier_4 (.a(bit_extender_1_out), .b(16'h4), .out(multiplier_4_out));  // open: cin, cout
  Multiplexer #(.width(16)) multiplexer_1 (
    .in0(multiplier_1_out), .in1(in_3), .out(multiplexer_1_out), .sel(in_2));  // open: en
  Adder #(.width(16)) adder_1 (.a(multiplier_2_out), .b(16'h1), .out(adder_1_out));  // open: cin, cout
  Multiplexer #(.width(16)) multiplexer_2 (
    .in0(adder_1_out), .in1(in_3), .out(multiplexer_2_out), .sel(in_2));  // open: en
  Adder #(.width(16)) adder_2 (.a(multiplier_3_out), .b(16'h2), .out(adder_2_out));  // open: cin, cout
  Multiplexer #(.width(16)) multiplexer_3 (
    .in0(adder_2_out), .in1(in_3), .out(multiplexer_3_out), .sel(in_2));  // open: en
  Adder #(.width(16)) adder_3 (.a(multiplier_4_out), .b(16'h3), .out(adder_3_out));  // open: cin, cout
  Multiplexer #(.width(16)) multiplexer_4 (
    .in0(adder_3_out), .in1(in_3), .out(multiplexer_4_out), .sel(in_2));  // open: en
  not not_1 (not_1_out, in_2);
  not not_2 (not_2_out, in_2);
  not not_3 (not_3_out, in_2);
  not not_4 (not_4_out, in_2);
  assign out_6 = in_2 ? in_1 : 8'bz;  // Controlled_Buffer controlled_buffer_1
  RAM #(.addrWidth(16)) ram_1 (.addr(multiplexer_1_out), .data(out_6), .clk(in_5), .ld(not_1_out));  // open: sel, clr
  assign out_7 = in_2 ? in_1 : 8'bz;  // Controlled_Buffer controlled_buffer_2
  RAM #(.addrWidth(16)) ram_2 (.addr(multiplexer_2_out), .data(out_7), .clk(in_5), .ld(not_2_out));  // open: sel, clr
  RAM #(.addrWidth(16)) ram_3 (.addr(multiplexer_3_out), .data(out_8), .clk(in_5), .ld(not_3_out));  // open: sel, clr
  assign out_8 = in_2 ? in_1 : 8'bz;  // Controlled_Buffer controlled_buffer_3
  assign out_9 = in_2 ? in_1 : 8'bz;  // Controlled_Buffer controlled_buffer_4
  RAM #(.addrWidth(16)) ram_4 (.addr(multiplexer_4_out), .data(out_9), .clk(in_5), .ld(not_4_out));  // open: sel, clr
endmodule

module Program_Counter (
  input  [13:0] in_1,
  input  in_2,
  input  in_3,
  input  in_4,
  output [13:0] out_5
);

  wire not_1_out;

  not not_1 (not_1_out, in_2);
  Counter #(.width(14), .max('h3fff)) counter_1 (
    .load(in_2), .D(in_1), .count(not_1_out), .Q(out_5), .clk(in_3), .clr(in_4));  // open: carry
endmodule

module Controll_Rom (
  input  [7:0] in_1,
  input  [7:0] in_2,
  input  [7:0] in_3,
  input  [7:0] in_4,
  output out_5,
  output [3:0] out_6,
  output out_7,
  output out_8,
  output out_9,
  output [3:0] out_10,
  output out_11,
  output [3:0] out_12,
  output [1:0] out_13,
  output [13:0] out_14,
  output [7:0] out_15,
  output [3:0] out_16
);

  wire and_3_out, and_4_out;
  wire [1:0] controlled_buffer_1_out;
  wire [5:5] rom_1_data;
  wire [7:0] controlled_buffer_5_out, controlled_buffer_6_out, controlled_buffer_7_out,
       controlled_buffer_8_out;

  ROM rom_1 (.addr(in_1), .data({out_11, out_8, rom_1_data[5], out_6, out_5}));  // open: sel
  assign {out_14[5:0], controlled_buffer_1_out} = out_8 ? in_2 : 8'bz;  // Controlled_Buffer controlled_buffer_1
  assign out_14[13:6] = out_8 ? in_3 : 8'bz;  // Controlled_Buffer controlled_buffer_2
  assign out_13 = out_11 ? controlled_buffer_1_out : 2'bz;  // Controlled_Buffer controlled_buffer_3
  assign out_15 = rom_1_data[5] ? in_3 : 8'bz;  // Controlled_Buffer controlled_buffer_4
  assign controlled_buffer_5_out = rom_1_data[5] ? in_2 : 8'bz;  // Controlled_Buffer controlled_buffer_5
  and and_1 (out_7, out_5, rom_1_data[5]);
  and and_2 (out_9, rom_1_data[5], ~out_5);  // AND_Gate
  and and_3 (and_3_out, rom_1_data[5], out_5);
  assign controlled_buffer_6_out = and_3_out ? in_2 : 8'bz;  // Controlled_Buffer controlled_buffer_6
  BitSelector #(.group(4)) bitselector_1 (.in(controlled_buffer_5_out), .out(out_16), .sel(1'b1));
  and and_4 (and_4_out, out_5, ~rom_1_data[5]);  // AND_Gate
  BitSelector #(.group(4)) bitselector_2 (.in(controlled_buffer_6_out), .out(out_10), .sel(1'b1));
  assign controlled_buffer_7_out = and_4_out ? in_2 : 8'bz;  // Controlled_Buffer controlled_buffer_7
  assign controlled_buffer_8_out = and_4_out ? in_3 : 8'bz;  // Controlled_Buffer controlled_buffer_8
  BitSelector #(.group(4)) bitselector_3 (.in(controlled_buffer_7_out), .out(out_10), .sel(1'b0));
  BitSelector #(.group(4)) bitselector_4 (.in(controlled_buffer_7_out), .out(out_12), .sel(1'b1));
  BitSelector #(.group(4)) bitselector_5 (.in(controlled_buffer_8_out), .out(out_16), .sel(1'b0));

  // Notes on the sheet:
  //   contents of rom_1 (hex, n*v repeats v):
  //   0 0 1 3 5 7 20 21 23 40 c0
endmodule

module Flag_Register (
  input  in_1,
  input  [3:0] in_2,
  input  [1:0] in_3,
  output out_4
);

  wire d_ff_1_q, d_ff_1_qn, d_ff_2_q, d_ff_2_qn;

  D_Flip_Flop d_ff_1 (.clk(in_1), .D(in_2[0]), .Q(d_ff_1_q), .Qn(d_ff_1_qn));  // open: preset, en, reset
  D_Flip_Flop d_ff_2 (.clk(in_1), .D(in_2[1]), .Q(d_ff_2_q), .Qn(d_ff_2_qn));  // open: preset, en, reset
  D_Flip_Flop d_ff_3 (.clk(in_1), .D(in_2[2]));  // open: Q, Qn, preset, en, reset
  D_Flip_Flop d_ff_4 (.clk(in_1), .D(in_2[3]));  // open: Q, Qn, preset, en, reset
  Multiplexer #(.select(2)) multiplexer_1 (
    .in0(d_ff_1_q), .in1(d_ff_1_qn), .in2(d_ff_2_q), .in3(d_ff_2_qn), .out(out_4), .sel(in_3));  // open: en
endmodule

module Bidirectional_Shift_Register (
  input  in_1,
  input  in_2,
  input  in_3,
  input  in_4,
  output out_5,
  output out_6,
  output out_7,
  output out_8,
  output out_9
);

  wire and_1_out, and_2_out, and_3_out, and_4_out, and_5_out, and_6_out, and_7_out, and_8_out, d_ff_2_q,
       d_ff_3_q, not_1_out, or_1_out, or_2_out, or_3_out, or_4_out;

  not not_1 (not_1_out, in_1);
  and and_1 (and_1_out, not_1_out, d_ff_2_q);
  and and_2 (and_2_out, in_2, in_1);
  or or_1 (or_1_out, and_2_out, and_1_out);
  and and_3 (and_3_out, out_9, in_1);
  or or_2 (or_2_out, and_3_out, and_4_out);
  D_Flip_Flop d_ff_1 (.clk(in_3), .D(or_1_out), .Q(out_9), .reset(in_4));  // open: Qn, preset, en
  and and_4 (and_4_out, not_1_out, d_ff_3_q);
  and and_5 (and_5_out, d_ff_2_q, in_1);
  D_Flip_Flop d_ff_2 (.clk(in_3), .D(or_2_out), .Q(d_ff_2_q), .reset(in_4));  // open: Qn, preset, en
  and and_6 (and_6_out, not_1_out, out_6);
  or or_3 (or_3_out, and_5_out, and_6_out);
  D_Flip_Flop d_ff_3 (.clk(in_3), .D(or_3_out), .Q(d_ff_3_q), .reset(in_4));  // open: Qn, preset, en
  and and_7 (and_7_out, d_ff_3_q, in_1);
  and and_8 (and_8_out, not_1_out, 1'b0);
  or or_4 (or_4_out, and_7_out, and_8_out);
  D_Flip_Flop d_ff_4 (.clk(in_3), .D(or_4_out), .Q(out_6), .reset(in_4));  // open: Qn, preset, en

  assign out_5 = in_1;
  assign out_7 = in_3;
  assign out_8 = in_4;
endmodule

module Multi_Bit_Bidirectional_Shift_Register (
  input  in_1,
  input  in_2,
  input  [13:0] in_3,
  input  in_4,
  output [13:0] out_5,
  output [13:0] out_6
);

  wire bidirectional_shift_register_1_out_5, bidirectional_shift_register_1_out_6,
       bidirectional_shift_register_1_out_7, bidirectional_shift_register_1_out_8,
       bidirectional_shift_register_2_out_5, bidirectional_shift_register_2_out_6,
       bidirectional_shift_register_2_out_7, bidirectional_shift_register_2_out_8,
       bidirectional_shift_register_3_out_5, bidirectional_shift_register_3_out_6,
       bidirectional_shift_register_3_out_7, bidirectional_shift_register_3_out_8,
       bidirectional_shift_register_4_out_5, bidirectional_shift_register_4_out_6,
       bidirectional_shift_register_4_out_7, bidirectional_shift_register_4_out_8,
       bidirectional_shift_register_5_out_5, bidirectional_shift_register_5_out_6,
       bidirectional_shift_register_5_out_7, bidirectional_shift_register_5_out_8,
       bidirectional_shift_register_6_out_5, bidirectional_shift_register_6_out_6,
       bidirectional_shift_register_6_out_7, bidirectional_shift_register_6_out_8,
       bidirectional_shift_register_7_out_5, bidirectional_shift_register_7_out_6,
       bidirectional_shift_register_7_out_7, bidirectional_shift_register_7_out_8,
       bidirectional_shift_register_8_out_5, bidirectional_shift_register_8_out_6,
       bidirectional_shift_register_8_out_7, bidirectional_shift_register_8_out_8,
       bidirectional_shift_register_9_out_5, bidirectional_shift_register_9_out_6,
       bidirectional_shift_register_9_out_7, bidirectional_shift_register_9_out_8,
       bidirectional_shift_register_10_out_5, bidirectional_shift_register_10_out_6,
       bidirectional_shift_register_10_out_7, bidirectional_shift_register_10_out_8,
       bidirectional_shift_register_11_out_5, bidirectional_shift_register_11_out_6,
       bidirectional_shift_register_11_out_7, bidirectional_shift_register_11_out_8,
       bidirectional_shift_register_12_out_5, bidirectional_shift_register_12_out_6,
       bidirectional_shift_register_12_out_7, bidirectional_shift_register_12_out_8,
       bidirectional_shift_register_13_out_5, bidirectional_shift_register_13_out_6,
       bidirectional_shift_register_13_out_7, bidirectional_shift_register_13_out_8,
       bidirectional_shift_register_14_out_5, bidirectional_shift_register_14_out_6,
       bidirectional_shift_register_14_out_7, bidirectional_shift_register_14_out_8,
       bidirectional_shift_register_15_out_5, bidirectional_shift_register_15_out_6,
       bidirectional_shift_register_15_out_7, bidirectional_shift_register_15_out_8,
       bidirectional_shift_register_16_out_5, bidirectional_shift_register_16_out_6,
       bidirectional_shift_register_16_out_7, bidirectional_shift_register_16_out_8,
       bidirectional_shift_register_17_out_5, bidirectional_shift_register_17_out_6,
       bidirectional_shift_register_17_out_7, bidirectional_shift_register_17_out_8,
       bidirectional_shift_register_18_out_5, bidirectional_shift_register_18_out_6,
       bidirectional_shift_register_18_out_7, bidirectional_shift_register_18_out_8,
       bidirectional_shift_register_19_out_5, bidirectional_shift_register_19_out_6,
       bidirectional_shift_register_19_out_7, bidirectional_shift_register_19_out_8,
       bidirectional_shift_register_20_out_5, bidirectional_shift_register_20_out_6,
       bidirectional_shift_register_20_out_7, bidirectional_shift_register_20_out_8,
       bidirectional_shift_register_21_out_5, bidirectional_shift_register_21_out_6,
       bidirectional_shift_register_21_out_7, bidirectional_shift_register_21_out_8,
       bidirectional_shift_register_22_out_5, bidirectional_shift_register_22_out_6,
       bidirectional_shift_register_22_out_7, bidirectional_shift_register_22_out_8,
       bidirectional_shift_register_23_out_5, bidirectional_shift_register_23_out_6,
       bidirectional_shift_register_23_out_7, bidirectional_shift_register_23_out_8,
       bidirectional_shift_register_24_out_5, bidirectional_shift_register_24_out_6,
       bidirectional_shift_register_24_out_7, bidirectional_shift_register_24_out_8,
       bidirectional_shift_register_25_out_5, bidirectional_shift_register_25_out_6,
       bidirectional_shift_register_25_out_7, bidirectional_shift_register_25_out_8,
       bidirectional_shift_register_26_out_5, bidirectional_shift_register_26_out_6,
       bidirectional_shift_register_26_out_7, bidirectional_shift_register_26_out_8,
       bidirectional_shift_register_27_out_5, bidirectional_shift_register_27_out_6,
       bidirectional_shift_register_27_out_7, bidirectional_shift_register_27_out_8,
       bidirectional_shift_register_28_out_5, bidirectional_shift_register_28_out_6,
       bidirectional_shift_register_28_out_7, bidirectional_shift_register_28_out_8,
       bidirectional_shift_register_29_out_5, bidirectional_shift_register_29_out_6,
       bidirectional_shift_register_29_out_7, bidirectional_shift_register_29_out_8,
       bidirectional_shift_register_30_out_5, bidirectional_shift_register_30_out_6,
       bidirectional_shift_register_30_out_7, bidirectional_shift_register_30_out_8,
       bidirectional_shift_register_31_out_5, bidirectional_shift_register_31_out_6,
       bidirectional_shift_register_31_out_7, bidirectional_shift_register_31_out_8,
       bidirectional_shift_register_32_out_5, bidirectional_shift_register_32_out_6,
       bidirectional_shift_register_32_out_7, bidirectional_shift_register_32_out_8,
       bidirectional_shift_register_33_out_5, bidirectional_shift_register_33_out_6,
       bidirectional_shift_register_33_out_7, bidirectional_shift_register_33_out_8,
       bidirectional_shift_register_34_out_5, bidirectional_shift_register_34_out_6,
       bidirectional_shift_register_34_out_7, bidirectional_shift_register_34_out_8,
       bidirectional_shift_register_35_out_5, bidirectional_shift_register_35_out_6,
       bidirectional_shift_register_35_out_7, bidirectional_shift_register_35_out_8,
       bidirectional_shift_register_36_out_5, bidirectional_shift_register_36_out_6,
       bidirectional_shift_register_36_out_7, bidirectional_shift_register_36_out_8,
       bidirectional_shift_register_37_out_5, bidirectional_shift_register_37_out_6,
       bidirectional_shift_register_37_out_7, bidirectional_shift_register_37_out_8,
       bidirectional_shift_register_38_out_5, bidirectional_shift_register_38_out_6,
       bidirectional_shift_register_38_out_7, bidirectional_shift_register_38_out_8,
       bidirectional_shift_register_39_out_5, bidirectional_shift_register_39_out_6,
       bidirectional_shift_register_39_out_7, bidirectional_shift_register_39_out_8,
       bidirectional_shift_register_40_out_5, bidirectional_shift_register_40_out_6,
       bidirectional_shift_register_40_out_7, bidirectional_shift_register_40_out_8,
       bidirectional_shift_register_41_out_5, bidirectional_shift_register_41_out_6,
       bidirectional_shift_register_41_out_7, bidirectional_shift_register_41_out_8,
       bidirectional_shift_register_42_out_5, bidirectional_shift_register_42_out_6,
       bidirectional_shift_register_42_out_7, bidirectional_shift_register_42_out_8,
       bidirectional_shift_register_43_out_5, bidirectional_shift_register_43_out_6,
       bidirectional_shift_register_43_out_7, bidirectional_shift_register_43_out_8,
       bidirectional_shift_register_44_out_5, bidirectional_shift_register_44_out_6,
       bidirectional_shift_register_44_out_7, bidirectional_shift_register_44_out_8,
       bidirectional_shift_register_45_out_5, bidirectional_shift_register_45_out_6,
       bidirectional_shift_register_45_out_7, bidirectional_shift_register_45_out_8,
       bidirectional_shift_register_46_out_5, bidirectional_shift_register_46_out_6,
       bidirectional_shift_register_46_out_7, bidirectional_shift_register_46_out_8,
       bidirectional_shift_register_47_out_5, bidirectional_shift_register_47_out_6,
       bidirectional_shift_register_47_out_7, bidirectional_shift_register_47_out_8,
       bidirectional_shift_register_48_out_5, bidirectional_shift_register_48_out_6,
       bidirectional_shift_register_48_out_7, bidirectional_shift_register_48_out_8,
       bidirectional_shift_register_49_out_5, bidirectional_shift_register_49_out_6,
       bidirectional_shift_register_49_out_7, bidirectional_shift_register_49_out_8,
       bidirectional_shift_register_50_out_5, bidirectional_shift_register_50_out_6,
       bidirectional_shift_register_50_out_7, bidirectional_shift_register_50_out_8,
       bidirectional_shift_register_51_out_5, bidirectional_shift_register_51_out_6,
       bidirectional_shift_register_51_out_7, bidirectional_shift_register_51_out_8,
       bidirectional_shift_register_52_out_5, bidirectional_shift_register_52_out_6,
       bidirectional_shift_register_52_out_7, bidirectional_shift_register_52_out_8,
       bidirectional_shift_register_53_out_5, bidirectional_shift_register_53_out_6,
       bidirectional_shift_register_53_out_7, bidirectional_shift_register_53_out_8,
       bidirectional_shift_register_54_out_5, bidirectional_shift_register_54_out_6,
       bidirectional_shift_register_54_out_7, bidirectional_shift_register_54_out_8,
       bidirectional_shift_register_55_out_5, bidirectional_shift_register_55_out_6,
       bidirectional_shift_register_55_out_7, bidirectional_shift_register_55_out_8,
       bidirectional_shift_register_56_out_5, bidirectional_shift_register_56_out_6,
       bidirectional_shift_register_56_out_7, bidirectional_shift_register_56_out_8,
       bidirectional_shift_register_57_out_5, bidirectional_shift_register_57_out_6,
       bidirectional_shift_register_57_out_7, bidirectional_shift_register_57_out_8,
       bidirectional_shift_register_58_out_5, bidirectional_shift_register_58_out_6,
       bidirectional_shift_register_58_out_7, bidirectional_shift_register_58_out_8,
       bidirectional_shift_register_59_out_5, bidirectional_shift_register_59_out_6,
       bidirectional_shift_register_59_out_7, bidirectional_shift_register_59_out_8,
       bidirectional_shift_register_60_out_5, bidirectional_shift_register_60_out_6,
       bidirectional_shift_register_60_out_7, bidirectional_shift_register_60_out_8,
       bidirectional_shift_register_61_out_5, bidirectional_shift_register_61_out_6,
       bidirectional_shift_register_61_out_7, bidirectional_shift_register_61_out_8,
       bidirectional_shift_register_62_out_5, bidirectional_shift_register_62_out_6,
       bidirectional_shift_register_62_out_7, bidirectional_shift_register_62_out_8,
       bidirectional_shift_register_63_out_5, bidirectional_shift_register_63_out_6,
       bidirectional_shift_register_63_out_7, bidirectional_shift_register_63_out_8,
       bidirectional_shift_register_64_out_5, bidirectional_shift_register_64_out_6,
       bidirectional_shift_register_64_out_7, bidirectional_shift_register_64_out_8,
       bidirectional_shift_register_65_out_5, bidirectional_shift_register_65_out_6,
       bidirectional_shift_register_65_out_7, bidirectional_shift_register_65_out_8,
       bidirectional_shift_register_66_out_5, bidirectional_shift_register_66_out_6,
       bidirectional_shift_register_66_out_7, bidirectional_shift_register_66_out_8,
       bidirectional_shift_register_67_out_5, bidirectional_shift_register_67_out_6,
       bidirectional_shift_register_67_out_7, bidirectional_shift_register_67_out_8,
       bidirectional_shift_register_68_out_5, bidirectional_shift_register_68_out_6,
       bidirectional_shift_register_68_out_7, bidirectional_shift_register_68_out_8,
       bidirectional_shift_register_69_out_5, bidirectional_shift_register_69_out_6,
       bidirectional_shift_register_69_out_7, bidirectional_shift_register_69_out_8,
       bidirectional_shift_register_70_out_5, bidirectional_shift_register_70_out_6,
       bidirectional_shift_register_70_out_7, bidirectional_shift_register_70_out_8,
       bidirectional_shift_register_71_out_5, bidirectional_shift_register_71_out_6,
       bidirectional_shift_register_71_out_7, bidirectional_shift_register_71_out_8,
       bidirectional_shift_register_72_out_5, bidirectional_shift_register_72_out_6,
       bidirectional_shift_register_72_out_7, bidirectional_shift_register_72_out_8,
       bidirectional_shift_register_73_out_5, bidirectional_shift_register_73_out_6,
       bidirectional_shift_register_73_out_7, bidirectional_shift_register_73_out_8,
       bidirectional_shift_register_74_out_5, bidirectional_shift_register_74_out_6,
       bidirectional_shift_register_74_out_7, bidirectional_shift_register_74_out_8,
       bidirectional_shift_register_75_out_5, bidirectional_shift_register_75_out_6,
       bidirectional_shift_register_75_out_7, bidirectional_shift_register_75_out_8,
       bidirectional_shift_register_76_out_5, bidirectional_shift_register_76_out_6,
       bidirectional_shift_register_76_out_7, bidirectional_shift_register_76_out_8,
       bidirectional_shift_register_77_out_5, bidirectional_shift_register_77_out_6,
       bidirectional_shift_register_77_out_7, bidirectional_shift_register_77_out_8,
       bidirectional_shift_register_78_out_5, bidirectional_shift_register_78_out_6,
       bidirectional_shift_register_78_out_7, bidirectional_shift_register_78_out_8,
       bidirectional_shift_register_79_out_5, bidirectional_shift_register_79_out_6,
       bidirectional_shift_register_79_out_7, bidirectional_shift_register_79_out_8,
       bidirectional_shift_register_80_out_5, bidirectional_shift_register_80_out_6,
       bidirectional_shift_register_80_out_7, bidirectional_shift_register_80_out_8,
       bidirectional_shift_register_81_out_5, bidirectional_shift_register_81_out_6,
       bidirectional_shift_register_81_out_7, bidirectional_shift_register_81_out_8,
       bidirectional_shift_register_82_out_5, bidirectional_shift_register_82_out_6,
       bidirectional_shift_register_82_out_7, bidirectional_shift_register_82_out_8,
       bidirectional_shift_register_83_out_5, bidirectional_shift_register_83_out_6,
       bidirectional_shift_register_83_out_7, bidirectional_shift_register_83_out_8,
       bidirectional_shift_register_84_out_5, bidirectional_shift_register_84_out_6,
       bidirectional_shift_register_84_out_7, bidirectional_shift_register_84_out_8,
       bidirectional_shift_register_85_out_5, bidirectional_shift_register_85_out_6,
       bidirectional_shift_register_85_out_7, bidirectional_shift_register_85_out_8,
       bidirectional_shift_register_86_out_5, bidirectional_shift_register_86_out_6,
       bidirectional_shift_register_86_out_7, bidirectional_shift_register_86_out_8,
       bidirectional_shift_register_87_out_5, bidirectional_shift_register_87_out_6,
       bidirectional_shift_register_87_out_7, bidirectional_shift_register_87_out_8,
       bidirectional_shift_register_88_out_5, bidirectional_shift_register_88_out_6,
       bidirectional_shift_register_88_out_7, bidirectional_shift_register_88_out_8,
       bidirectional_shift_register_89_out_5, bidirectional_shift_register_89_out_6,
       bidirectional_shift_register_89_out_7, bidirectional_shift_register_89_out_8,
       bidirectional_shift_register_90_out_5, bidirectional_shift_register_90_out_6,
       bidirectional_shift_register_90_out_7, bidirectional_shift_register_90_out_8,
       bidirectional_shift_register_91_out_5, bidirectional_shift_register_91_out_6,
       bidirectional_shift_register_91_out_7, bidirectional_shift_register_91_out_8,
       bidirectional_shift_register_92_out_5, bidirectional_shift_register_92_out_6,
       bidirectional_shift_register_92_out_7, bidirectional_shift_register_92_out_8,
       bidirectional_shift_register_93_out_5, bidirectional_shift_register_93_out_6,
       bidirectional_shift_register_93_out_7, bidirectional_shift_register_93_out_8,
       bidirectional_shift_register_94_out_5, bidirectional_shift_register_94_out_6,
       bidirectional_shift_register_94_out_7, bidirectional_shift_register_94_out_8,
       bidirectional_shift_register_95_out_5, bidirectional_shift_register_95_out_6,
       bidirectional_shift_register_95_out_7, bidirectional_shift_register_95_out_8,
       bidirectional_shift_register_96_out_5, bidirectional_shift_register_96_out_6,
       bidirectional_shift_register_96_out_7, bidirectional_shift_register_96_out_8,
       bidirectional_shift_register_97_out_5, bidirectional_shift_register_97_out_6,
       bidirectional_shift_register_97_out_7, bidirectional_shift_register_97_out_8,
       bidirectional_shift_register_98_out_5, bidirectional_shift_register_98_out_6,
       bidirectional_shift_register_98_out_7, bidirectional_shift_register_98_out_8;

  Bidirectional_Shift_Register bidirectional_shift_register_1 (
    .in_1(bidirectional_shift_register_2_out_5), .in_2(bidirectional_shift_register_2_out_6),
    .in_3(bidirectional_shift_register_2_out_7), .in_4(bidirectional_shift_register_2_out_8),
    .out_5(bidirectional_shift_register_1_out_5), .out_6(bidirectional_shift_register_1_out_6),
    .out_7(bidirectional_shift_register_1_out_7), .out_8(bidirectional_shift_register_1_out_8));  // open: out_9
  Bidirectional_Shift_Register bidirectional_shift_register_2 (
    .in_1(in_1), .in_2(in_3[0]), .in_3(in_2), .in_4(in_4), .out_5(bidirectional_shift_register_2_out_5),
    .out_6(bidirectional_shift_register_2_out_6), .out_7(bidirectional_shift_register_2_out_7),
    .out_9(out_6[0]), .out_8(bidirectional_shift_register_2_out_8));
  Bidirectional_Shift_Register bidirectional_shift_register_3 (
    .in_1(bidirectional_shift_register_4_out_5), .in_2(bidirectional_shift_register_4_out_6),
    .in_3(bidirectional_shift_register_4_out_7), .in_4(bidirectional_shift_register_4_out_8),
    .out_5(bidirectional_shift_register_3_out_5), .out_6(bidirectional_shift_register_3_out_6),
    .out_7(bidirectional_shift_register_3_out_7), .out_8(bidirectional_shift_register_3_out_8));  // open: out_9
  Bidirectional_Shift_Register bidirectional_shift_register_4 (
    .in_1(in_1), .in_2(in_3[1]), .in_3(in_2), .in_4(in_4), .out_5(bidirectional_shift_register_4_out_5),
    .out_6(bidirectional_shift_register_4_out_6), .out_7(bidirectional_shift_register_4_out_7),
    .out_9(out_6[1]), .out_8(bidirectional_shift_register_4_out_8));
  Bidirectional_Shift_Register bidirectional_shift_register_5 (
    .in_1(in_1), .in_2(in_3[2]), .in_3(in_2), .in_4(in_4), .out_5(bidirectional_shift_register_5_out_5),
    .out_6(bidirectional_shift_register_5_out_6), .out_7(bidirectional_shift_register_5_out_7),
    .out_9(out_6[2]), .out_8(bidirectional_shift_register_5_out_8));
  Bidirectional_Shift_Register bidirectional_shift_register_6 (
    .in_1(bidirectional_shift_register_5_out_5), .in_2(bidirectional_shift_register_5_out_6),
    .in_3(bidirectional_shift_register_5_out_7), .in_4(bidirectional_shift_register_5_out_8),
    .out_5(bidirectional_shift_register_6_out_5), .out_6(bidirectional_shift_register_6_out_6),
    .out_7(bidirectional_shift_register_6_out_7), .out_8(bidirectional_shift_register_6_out_8));  // open: out_9
  Bidirectional_Shift_Register bidirectional_shift_register_7 (
    .in_1(bidirectional_shift_register_8_out_5), .in_2(bidirectional_shift_register_8_out_6),
    .in_3(bidirectional_shift_register_8_out_7), .in_4(bidirectional_shift_register_8_out_8),
    .out_5(bidirectional_shift_register_7_out_5), .out_6(bidirectional_shift_register_7_out_6),
    .out_7(bidirectional_shift_register_7_out_7), .out_8(bidirectional_shift_register_7_out_8));  // open: out_9
  Bidirectional_Shift_Register bidirectional_shift_register_8 (
    .in_1(in_1), .in_2(in_3[3]), .in_3(in_2), .in_4(in_4), .out_5(bidirectional_shift_register_8_out_5),
    .out_6(bidirectional_shift_register_8_out_6), .out_7(bidirectional_shift_register_8_out_7),
    .out_9(out_6[3]), .out_8(bidirectional_shift_register_8_out_8));
  Bidirectional_Shift_Register bidirectional_shift_register_9 (
    .in_1(bidirectional_shift_register_10_out_5), .in_2(bidirectional_shift_register_10_out_6),
    .in_3(bidirectional_shift_register_10_out_7), .in_4(bidirectional_shift_register_10_out_8),
    .out_5(bidirectional_shift_register_9_out_5), .out_6(bidirectional_shift_register_9_out_6),
    .out_7(bidirectional_shift_register_9_out_7), .out_8(bidirectional_shift_register_9_out_8));  // open: out_9
  Bidirectional_Shift_Register bidirectional_shift_register_10 (
    .in_1(in_1), .in_2(in_3[4]), .in_3(in_2), .in_4(in_4), .out_5(bidirectional_shift_register_10_out_5),
    .out_6(bidirectional_shift_register_10_out_6), .out_7(bidirectional_shift_register_10_out_7),
    .out_9(out_6[4]), .out_8(bidirectional_shift_register_10_out_8));
  Bidirectional_Shift_Register bidirectional_shift_register_11 (
    .in_1(bidirectional_shift_register_12_out_5), .in_2(bidirectional_shift_register_12_out_6),
    .in_3(bidirectional_shift_register_12_out_7), .in_4(bidirectional_shift_register_12_out_8),
    .out_5(bidirectional_shift_register_11_out_5), .out_6(bidirectional_shift_register_11_out_6),
    .out_7(bidirectional_shift_register_11_out_7), .out_8(bidirectional_shift_register_11_out_8));  // open: out_9
  Bidirectional_Shift_Register bidirectional_shift_register_12 (
    .in_1(in_1), .in_2(in_3[5]), .in_3(in_2), .in_4(in_4), .out_5(bidirectional_shift_register_12_out_5),
    .out_6(bidirectional_shift_register_12_out_6), .out_7(bidirectional_shift_register_12_out_7),
    .out_9(out_6[5]), .out_8(bidirectional_shift_register_12_out_8));
  Bidirectional_Shift_Register bidirectional_shift_register_13 (
    .in_1(bidirectional_shift_register_14_out_5), .in_2(bidirectional_shift_register_14_out_6),
    .in_3(bidirectional_shift_register_14_out_7), .in_4(bidirectional_shift_register_14_out_8),
    .out_5(bidirectional_shift_register_13_out_5), .out_6(bidirectional_shift_register_13_out_6),
    .out_7(bidirectional_shift_register_13_out_7), .out_8(bidirectional_shift_register_13_out_8));  // open: out_9
  Bidirectional_Shift_Register bidirectional_shift_register_14 (
    .in_1(in_1), .in_2(in_3[6]), .in_3(in_2), .in_4(in_4), .out_5(bidirectional_shift_register_14_out_5),
    .out_6(bidirectional_shift_register_14_out_6), .out_7(bidirectional_shift_register_14_out_7),
    .out_9(out_6[6]), .out_8(bidirectional_shift_register_14_out_8));
  Bidirectional_Shift_Register bidirectional_shift_register_15 (
    .in_1(in_1), .in_2(in_3[7]), .in_3(in_2), .in_4(in_4), .out_5(bidirectional_shift_register_15_out_5),
    .out_6(bidirectional_shift_register_15_out_6), .out_7(bidirectional_shift_register_15_out_7),
    .out_9(out_6[7]), .out_8(bidirectional_shift_register_15_out_8));
  Bidirectional_Shift_Register bidirectional_shift_register_16 (
    .in_1(bidirectional_shift_register_15_out_5), .in_2(bidirectional_shift_register_15_out_6),
    .in_3(bidirectional_shift_register_15_out_7), .in_4(bidirectional_shift_register_15_out_8),
    .out_5(bidirectional_shift_register_16_out_5), .out_6(bidirectional_shift_register_16_out_6),
    .out_7(bidirectional_shift_register_16_out_7), .out_8(bidirectional_shift_register_16_out_8));  // open: out_9
  Bidirectional_Shift_Register bidirectional_shift_register_17 (
    .in_1(bidirectional_shift_register_18_out_5), .in_2(bidirectional_shift_register_18_out_6),
    .in_3(bidirectional_shift_register_18_out_7), .in_4(bidirectional_shift_register_18_out_8),
    .out_5(bidirectional_shift_register_17_out_5), .out_6(bidirectional_shift_register_17_out_6),
    .out_7(bidirectional_shift_register_17_out_7), .out_8(bidirectional_shift_register_17_out_8));  // open: out_9
  Bidirectional_Shift_Register bidirectional_shift_register_18 (
    .in_1(in_1), .in_2(in_3[8]), .in_3(in_2), .in_4(in_4), .out_5(bidirectional_shift_register_18_out_5),
    .out_6(bidirectional_shift_register_18_out_6), .out_7(bidirectional_shift_register_18_out_7),
    .out_9(out_6[8]), .out_8(bidirectional_shift_register_18_out_8));
  Bidirectional_Shift_Register bidirectional_shift_register_19 (
    .in_1(in_1), .in_2(in_3[9]), .in_3(in_2), .in_4(in_4), .out_5(bidirectional_shift_register_19_out_5),
    .out_6(bidirectional_shift_register_19_out_6), .out_7(bidirectional_shift_register_19_out_7),
    .out_9(out_6[9]), .out_8(bidirectional_shift_register_19_out_8));
  Bidirectional_Shift_Register bidirectional_shift_register_20 (
    .in_1(bidirectional_shift_register_19_out_5), .in_2(bidirectional_shift_register_19_out_6),
    .in_3(bidirectional_shift_register_19_out_7), .in_4(bidirectional_shift_register_19_out_8),
    .out_5(bidirectional_shift_register_20_out_5), .out_6(bidirectional_shift_register_20_out_6),
    .out_7(bidirectional_shift_register_20_out_7), .out_8(bidirectional_shift_register_20_out_8));  // open: out_9
  Bidirectional_Shift_Register bidirectional_shift_register_21 (
    .in_1(in_1), .in_2(in_3[10]), .in_3(in_2), .in_4(in_4), .out_5(bidirectional_shift_register_21_out_5),
    .out_6(bidirectional_shift_register_21_out_6), .out_7(bidirectional_shift_register_21_out_7),
    .out_9(out_6[10]), .out_8(bidirectional_shift_register_21_out_8));
  Bidirectional_Shift_Register bidirectional_shift_register_22 (
    .in_1(bidirectional_shift_register_21_out_5), .in_2(bidirectional_shift_register_21_out_6),
    .in_3(bidirectional_shift_register_21_out_7), .in_4(bidirectional_shift_register_21_out_8),
    .out_5(bidirectional_shift_register_22_out_5), .out_6(bidirectional_shift_register_22_out_6),
    .out_7(bidirectional_shift_register_22_out_7), .out_8(bidirectional_shift_register_22_out_8));  // open: out_9
  Bidirectional_Shift_Register bidirectional_shift_register_23 (
    .in_1(in_1), .in_2(in_3[11]), .in_3(in_2), .in_4(in_4), .out_5(bidirectional_shift_register_23_out_5),
    .out_6(bidirectional_shift_register_23_out_6), .out_7(bidirectional_shift_register_23_out_7),
    .out_9(out_6[11]), .out_8(bidirectional_shift_register_23_out_8));
  Bidirectional_Shift_Register bidirectional_shift_register_24 (
    .in_1(bidirectional_shift_register_23_out_5), .in_2(bidirectional_shift_register_23_out_6),
    .in_3(bidirectional_shift_register_23_out_7), .in_4(bidirectional_shift_register_23_out_8),
    .out_5(bidirectional_shift_register_24_out_5), .out_6(bidirectional_shift_register_24_out_6),
    .out_7(bidirectional_shift_register_24_out_7), .out_8(bidirectional_shift_register_24_out_8));  // open: out_9
  Bidirectional_Shift_Register bidirectional_shift_register_25 (
    .in_1(in_1), .in_2(in_3[12]), .in_3(in_2), .in_4(in_4), .out_5(bidirectional_shift_register_25_out_5),
    .out_6(bidirectional_shift_register_25_out_6), .out_7(bidirectional_shift_register_25_out_7),
    .out_9(out_6[12]), .out_8(bidirectional_shift_register_25_out_8));
  Bidirectional_Shift_Register bidirectional_shift_register_26 (
    .in_1(bidirectional_shift_register_25_out_5), .in_2(bidirectional_shift_register_25_out_6),
    .in_3(bidirectional_shift_register_25_out_7), .in_4(bidirectional_shift_register_25_out_8),
    .out_5(bidirectional_shift_register_26_out_5), .out_6(bidirectional_shift_register_26_out_6),
    .out_7(bidirectional_shift_register_26_out_7), .out_8(bidirectional_shift_register_26_out_8));  // open: out_9
  Bidirectional_Shift_Register bidirectional_shift_register_27 (
    .in_1(bidirectional_shift_register_28_out_5), .in_2(bidirectional_shift_register_28_out_6),
    .in_3(bidirectional_shift_register_28_out_7), .in_4(bidirectional_shift_register_28_out_8),
    .out_5(bidirectional_shift_register_27_out_5), .out_6(bidirectional_shift_register_27_out_6),
    .out_7(bidirectional_shift_register_27_out_7), .out_8(bidirectional_shift_register_27_out_8));  // open: out_9
  Bidirectional_Shift_Register bidirectional_shift_register_28 (
    .in_1(in_1), .in_2(in_3[13]), .in_3(in_2), .in_4(in_4), .out_5(bidirectional_shift_register_28_out_5),
    .out_6(bidirectional_shift_register_28_out_6), .out_7(bidirectional_shift_register_28_out_7),
    .out_9(out_6[13]), .out_8(bidirectional_shift_register_28_out_8));
  Bidirectional_Shift_Register bidirectional_shift_register_29 (
    .in_1(bidirectional_shift_register_30_out_5), .in_2(bidirectional_shift_register_30_out_6),
    .in_3(bidirectional_shift_register_30_out_7), .in_4(bidirectional_shift_register_30_out_8),
    .out_5(bidirectional_shift_register_29_out_5), .out_6(bidirectional_shift_register_29_out_6),
    .out_7(bidirectional_shift_register_29_out_7), .out_8(bidirectional_shift_register_29_out_8));  // open: out_9
  Bidirectional_Shift_Register bidirectional_shift_register_30 (
    .in_1(bidirectional_shift_register_1_out_5), .in_2(bidirectional_shift_register_1_out_6),
    .in_3(bidirectional_shift_register_1_out_7), .in_4(bidirectional_shift_register_1_out_8),
    .out_5(bidirectional_shift_register_30_out_5), .out_6(bidirectional_shift_register_30_out_6),
    .out_7(bidirectional_shift_register_30_out_7), .out_8(bidirectional_shift_register_30_out_8));  // open: out_9
  Bidirectional_Shift_Register bidirectional_shift_register_31 (
    .in_1(bidirectional_shift_register_32_out_5), .in_2(bidirectional_shift_register_32_out_6),
    .in_3(bidirectional_shift_register_32_out_7), .in_4(bidirectional_shift_register_32_out_8),
    .out_5(bidirectional_shift_register_31_out_5), .out_6(bidirectional_shift_register_31_out_6),
    .out_7(bidirectional_shift_register_31_out_7), .out_8(bidirectional_shift_register_31_out_8));  // open: out_9
  Bidirectional_Shift_Register bidirectional_shift_register_32 (
    .in_1(bidirectional_shift_register_3_out_5), .in_2(bidirectional_shift_register_3_out_6),
    .in_3(bidirectional_shift_register_3_out_7), .in_4(bidirectional_shift_register_3_out_8),
    .out_5(bidirectional_shift_register_32_out_5), .out_6(bidirectional_shift_register_32_out_6),
    .out_7(bidirectional_shift_register_32_out_7), .out_8(bidirectional_shift_register_32_out_8));  // open: out_9
  Bidirectional_Shift_Register bidirectional_shift_register_33 (
    .in_1(bidirectional_shift_register_6_out_5), .in_2(bidirectional_shift_register_6_out_6),
    .in_3(bidirectional_shift_register_6_out_7), .in_4(bidirectional_shift_register_6_out_8),
    .out_5(bidirectional_shift_register_33_out_5), .out_6(bidirectional_shift_register_33_out_6),
    .out_7(bidirectional_shift_register_33_out_7), .out_8(bidirectional_shift_register_33_out_8));  // open: out_9
  Bidirectional_Shift_Register bidirectional_shift_register_34 (
    .in_1(bidirectional_shift_register_33_out_5), .in_2(bidirectional_shift_register_33_out_6),
    .in_3(bidirectional_shift_register_33_out_7), .in_4(bidirectional_shift_register_33_out_8),
    .out_5(bidirectional_shift_register_34_out_5), .out_6(bidirectional_shift_register_34_out_6),
    .out_7(bidirectional_shift_register_34_out_7), .out_8(bidirectional_shift_register_34_out_8));  // open: out_9
  Bidirectional_Shift_Register bidirectional_shift_register_35 (
    .in_1(bidirectional_shift_register_36_out_5), .in_2(bidirectional_shift_register_36_out_6),
    .in_3(bidirectional_shift_register_36_out_7), .in_4(bidirectional_shift_register_36_out_8),
    .out_5(bidirectional_shift_register_35_out_5), .out_6(bidirectional_shift_register_35_out_6),
    .out_7(bidirectional_shift_register_35_out_7), .out_8(bidirectional_shift_register_35_out_8));  // open: out_9
  Bidirectional_Shift_Register bidirectional_shift_register_36 (
    .in_1(bidirectional_shift_register_7_out_5), .in_2(bidirectional_shift_register_7_out_6),
    .in_3(bidirectional_shift_register_7_out_7), .in_4(bidirectional_shift_register_7_out_8),
    .out_5(bidirectional_shift_register_36_out_5), .out_6(bidirectional_shift_register_36_out_6),
    .out_7(bidirectional_shift_register_36_out_7), .out_8(bidirectional_shift_register_36_out_8));  // open: out_9
  Bidirectional_Shift_Register bidirectional_shift_register_37 (
    .in_1(bidirectional_shift_register_9_out_5), .in_2(bidirectional_shift_register_9_out_6),
    .in_3(bidirectional_shift_register_9_out_7), .in_4(bidirectional_shift_register_9_out_8),
    .out_5(bidirectional_shift_register_37_out_5), .out_6(bidirectional_shift_register_37_out_6),
    .out_7(bidirectional_shift_register_37_out_7), .out_8(bidirectional_shift_register_37_out_8));  // open: out_9
  Bidirectional_Shift_Register bidirectional_shift_register_38 (
    .in_1(bidirectional_shift_register_37_out_5), .in_2(bidirectional_shift_register_37_out_6),
    .in_3(bidirectional_shift_register_37_out_7), .in_4(bidirectional_shift_register_37_out_8),
    .out_5(bidirectional_shift_register_38_out_5), .out_6(bidirectional_shift_register_38_out_6),
    .out_7(bidirectional_shift_register_38_out_7), .out_8(bidirectional_shift_register_38_out_8));  // open: out_9
  Bidirectional_Shift_Register bidirectional_shift_register_39 (
    .in_1(bidirectional_shift_register_11_out_5), .in_2(bidirectional_shift_register_11_out_6),
    .in_3(bidirectional_shift_register_11_out_7), .in_4(bidirectional_shift_register_11_out_8),
    .out_5(bidirectional_shift_register_39_out_5), .out_6(bidirectional_shift_register_39_out_6),
    .out_7(bidirectional_shift_register_39_out_7), .out_8(bidirectional_shift_register_39_out_8));  // open: out_9
  Bidirectional_Shift_Register bidirectional_shift_register_40 (
    .in_1(bidirectional_shift_register_39_out_5), .in_2(bidirectional_shift_register_39_out_6),
    .in_3(bidirectional_shift_register_39_out_7), .in_4(bidirectional_shift_register_39_out_8),
    .out_5(bidirectional_shift_register_40_out_5), .out_6(bidirectional_shift_register_40_out_6),
    .out_7(bidirectional_shift_register_40_out_7), .out_8(bidirectional_shift_register_40_out_8));  // open: out_9
  Bidirectional_Shift_Register bidirectional_shift_register_41 (
    .in_1(bidirectional_shift_register_42_out_5), .in_2(bidirectional_shift_register_42_out_6),
    .in_3(bidirectional_shift_register_42_out_7), .in_4(bidirectional_shift_register_42_out_8),
    .out_5(bidirectional_shift_register_41_out_5), .out_6(bidirectional_shift_register_41_out_6),
    .out_7(bidirectional_shift_register_41_out_7), .out_8(bidirectional_shift_register_41_out_8));  // open: out_9
  Bidirectional_Shift_Register bidirectional_shift_register_42 (
    .in_1(bidirectional_shift_register_13_out_5), .in_2(bidirectional_shift_register_13_out_6),
    .in_3(bidirectional_shift_register_13_out_7), .in_4(bidirectional_shift_register_13_out_8),
    .out_5(bidirectional_shift_register_42_out_5), .out_6(bidirectional_shift_register_42_out_6),
    .out_7(bidirectional_shift_register_42_out_7), .out_8(bidirectional_shift_register_42_out_8));  // open: out_9
  Bidirectional_Shift_Register bidirectional_shift_register_43 (
    .in_1(bidirectional_shift_register_16_out_5), .in_2(bidirectional_shift_register_16_out_6),
    .in_3(bidirectional_shift_register_16_out_7), .in_4(bidirectional_shift_register_16_out_8),
    .out_5(bidirectional_shift_register_43_out_5), .out_6(bidirectional_shift_register_43_out_6),
    .out_7(bidirectional_shift_register_43_out_7), .out_8(bidirectional_shift_register_43_out_8));  // open: out_9
  Bidirectional_Shift_Register bidirectional_shift_register_44 (
    .in_1(bidirectional_shift_register_43_out_5), .in_2(bidirectional_shift_register_43_out_6),
    .in_3(bidirectional_shift_register_43_out_7), .in_4(bidirectional_shift_register_43_out_8),
    .out_5(bidirectional_shift_register_44_out_5), .out_6(bidirectional_shift_register_44_out_6),
    .out_7(bidirectional_shift_register_44_out_7), .out_8(bidirectional_shift_register_44_out_8));  // open: out_9
  Bidirectional_Shift_Register bidirectional_shift_register_45 (
    .in_1(bidirectional_shift_register_17_out_5), .in_2(bidirectional_shift_register_17_out_6),
    .in_3(bidirectional_shift_register_17_out_7), .in_4(bidirectional_shift_register_17_out_8),
    .out_5(bidirectional_shift_register_45_out_5), .out_6(bidirectional_shift_register_45_out_6),
    .out_7(bidirectional_shift_register_45_out_7), .out_8(bidirectional_shift_register_45_out_8));  // open: out_9
  Bidirectional_Shift_Register bidirectional_shift_register_46 (
    .in_1(bidirectional_shift_register_45_out_5), .in_2(bidirectional_shift_register_45_out_6),
    .in_3(bidirectional_shift_register_45_out_7), .in_4(bidirectional_shift_register_45_out_8),
    .out_5(bidirectional_shift_register_46_out_5), .out_6(bidirectional_shift_register_46_out_6),
    .out_7(bidirectional_shift_register_46_out_7), .out_8(bidirectional_shift_register_46_out_8));  // open: out_9
  Bidirectional_Shift_Register bidirectional_shift_register_47 (
    .in_1(bidirectional_shift_register_20_out_5), .in_2(bidirectional_shift_register_20_out_6),
    .in_3(bidirectional_shift_register_20_out_7), .in_4(bidirectional_shift_register_20_out_8),
    .out_5(bidirectional_shift_register_47_out_5), .out_6(bidirectional_shift_register_47_out_6),
    .out_7(bidirectional_shift_register_47_out_7), .out_8(bidirectional_shift_register_47_out_8));  // open: out_9
  Bidirectional_Shift_Register bidirectional_shift_register_48 (
    .in_1(bidirectional_shift_register_47_out_5), .in_2(bidirectional_shift_register_47_out_6),
    .in_3(bidirectional_shift_register_47_out_7), .in_4(bidirectional_shift_register_47_out_8),
    .out_5(bidirectional_shift_register_48_out_5), .out_6(bidirectional_shift_register_48_out_6),
    .out_7(bidirectional_shift_register_48_out_7), .out_8(bidirectional_shift_register_48_out_8));  // open: out_9
  Bidirectional_Shift_Register bidirectional_shift_register_49 (
    .in_1(bidirectional_shift_register_50_out_5), .in_2(bidirectional_shift_register_50_out_6),
    .in_3(bidirectional_shift_register_50_out_7), .in_4(bidirectional_shift_register_50_out_8),
    .out_5(bidirectional_shift_register_49_out_5), .out_6(bidirectional_shift_register_49_out_6),
    .out_7(bidirectional_shift_register_49_out_7), .out_8(bidirectional_shift_register_49_out_8));  // open: out_9
  Bidirectional_Shift_Register bidirectional_shift_register_50 (
    .in_1(bidirectional_shift_register_22_out_5), .in_2(bidirectional_shift_register_22_out_6),
    .in_3(bidirectional_shift_register_22_out_7), .in_4(bidirectional_shift_register_22_out_8),
    .out_5(bidirectional_shift_register_50_out_5), .out_6(bidirectional_shift_register_50_out_6),
    .out_7(bidirectional_shift_register_50_out_7), .out_8(bidirectional_shift_register_50_out_8));  // open: out_9
  Bidirectional_Shift_Register bidirectional_shift_register_51 (
    .in_1(bidirectional_shift_register_52_out_5), .in_2(bidirectional_shift_register_52_out_6),
    .in_3(bidirectional_shift_register_52_out_7), .in_4(bidirectional_shift_register_52_out_8),
    .out_5(bidirectional_shift_register_51_out_5), .out_6(bidirectional_shift_register_51_out_6),
    .out_7(bidirectional_shift_register_51_out_7), .out_8(bidirectional_shift_register_51_out_8));  // open: out_9
  Bidirectional_Shift_Register bidirectional_shift_register_52 (
    .in_1(bidirectional_shift_register_24_out_5), .in_2(bidirectional_shift_register_24_out_6),
    .in_3(bidirectional_shift_register_24_out_7), .in_4(bidirectional_shift_register_24_out_8),
    .out_5(bidirectional_shift_register_52_out_5), .out_6(bidirectional_shift_register_52_out_6),
    .out_7(bidirectional_shift_register_52_out_7), .out_8(bidirectional_shift_register_52_out_8));  // open: out_9
  Bidirectional_Shift_Register bidirectional_shift_register_53 (
    .in_1(bidirectional_shift_register_26_out_5), .in_2(bidirectional_shift_register_26_out_6),
    .in_3(bidirectional_shift_register_26_out_7), .in_4(bidirectional_shift_register_26_out_8),
    .out_5(bidirectional_shift_register_53_out_5), .out_6(bidirectional_shift_register_53_out_6),
    .out_7(bidirectional_shift_register_53_out_7), .out_8(bidirectional_shift_register_53_out_8));  // open: out_9
  Bidirectional_Shift_Register bidirectional_shift_register_54 (
    .in_1(bidirectional_shift_register_53_out_5), .in_2(bidirectional_shift_register_53_out_6),
    .in_3(bidirectional_shift_register_53_out_7), .in_4(bidirectional_shift_register_53_out_8),
    .out_5(bidirectional_shift_register_54_out_5), .out_6(bidirectional_shift_register_54_out_6),
    .out_7(bidirectional_shift_register_54_out_7), .out_8(bidirectional_shift_register_54_out_8));  // open: out_9
  Bidirectional_Shift_Register bidirectional_shift_register_55 (
    .in_1(bidirectional_shift_register_27_out_5), .in_2(bidirectional_shift_register_27_out_6),
    .in_3(bidirectional_shift_register_27_out_7), .in_4(bidirectional_shift_register_27_out_8),
    .out_5(bidirectional_shift_register_55_out_5), .out_6(bidirectional_shift_register_55_out_6),
    .out_7(bidirectional_shift_register_55_out_7), .out_8(bidirectional_shift_register_55_out_8));  // open: out_9
  Bidirectional_Shift_Register bidirectional_shift_register_56 (
    .in_1(bidirectional_shift_register_55_out_5), .in_2(bidirectional_shift_register_55_out_6),
    .in_3(bidirectional_shift_register_55_out_7), .in_4(bidirectional_shift_register_55_out_8),
    .out_5(bidirectional_shift_register_56_out_5), .out_6(bidirectional_shift_register_56_out_6),
    .out_7(bidirectional_shift_register_56_out_7), .out_8(bidirectional_shift_register_56_out_8));  // open: out_9
  Bidirectional_Shift_Register bidirectional_shift_register_57 (
    .in_1(bidirectional_shift_register_59_out_5), .in_2(bidirectional_shift_register_59_out_6),
    .in_3(bidirectional_shift_register_59_out_7), .in_4(bidirectional_shift_register_59_out_8),
    .out_5(bidirectional_shift_register_57_out_5), .out_6(bidirectional_shift_register_57_out_6),
    .out_7(bidirectional_shift_register_57_out_7), .out_8(bidirectional_shift_register_57_out_8));  // open: out_9
  Bidirectional_Shift_Register bidirectional_shift_register_58 (
    .in_1(bidirectional_shift_register_57_out_5), .in_2(bidirectional_shift_register_57_out_6),
    .in_3(bidirectional_shift_register_57_out_7), .in_4(bidirectional_shift_register_57_out_8),
    .out_5(bidirectional_shift_register_58_out_5), .out_6(bidirectional_shift_register_58_out_6),
    .out_7(bidirectional_shift_register_58_out_7), .out_8(bidirectional_shift_register_58_out_8));  // open: out_9
  Bidirectional_Shift_Register bidirectional_shift_register_59 (
    .in_1(bidirectional_shift_register_29_out_5), .in_2(bidirectional_shift_register_29_out_6),
    .in_3(bidirectional_shift_register_29_out_7), .in_4(bidirectional_shift_register_29_out_8),
    .out_5(bidirectional_shift_register_59_out_5), .out_6(bidirectional_shift_register_59_out_6),
    .out_7(bidirectional_shift_register_59_out_7), .out_8(bidirectional_shift_register_59_out_8));  // open: out_9
  Bidirectional_Shift_Register bidirectional_shift_register_60 (
    .in_1(bidirectional_shift_register_61_out_5), .in_2(bidirectional_shift_register_61_out_6),
    .in_3(bidirectional_shift_register_61_out_7), .in_4(bidirectional_shift_register_61_out_8),
    .out_5(bidirectional_shift_register_60_out_5), .out_6(bidirectional_shift_register_60_out_6),
    .out_7(bidirectional_shift_register_60_out_7), .out_8(bidirectional_shift_register_60_out_8));  // open: out_9
  Bidirectional_Shift_Register bidirectional_shift_register_61 (
    .in_1(bidirectional_shift_register_31_out_5), .in_2(bidirectional_shift_register_31_out_6),
    .in_3(bidirectional_shift_register_31_out_7), .in_4(bidirectional_shift_register_31_out_8),
    .out_5(bidirectional_shift_register_61_out_5), .out_6(bidirectional_shift_register_61_out_6),
    .out_7(bidirectional_shift_register_61_out_7), .out_8(bidirectional_shift_register_61_out_8));  // open: out_9
  Bidirectional_Shift_Register bidirectional_shift_register_62 (
    .in_1(bidirectional_shift_register_60_out_5), .in_2(bidirectional_shift_register_60_out_6),
    .in_3(bidirectional_shift_register_60_out_7), .in_4(bidirectional_shift_register_60_out_8),
    .out_5(bidirectional_shift_register_62_out_5), .out_6(bidirectional_shift_register_62_out_6),
    .out_7(bidirectional_shift_register_62_out_7), .out_8(bidirectional_shift_register_62_out_8));  // open: out_9
  Bidirectional_Shift_Register bidirectional_shift_register_63 (
    .in_1(bidirectional_shift_register_64_out_5), .in_2(bidirectional_shift_register_64_out_6),
    .in_3(bidirectional_shift_register_64_out_7), .in_4(bidirectional_shift_register_64_out_8),
    .out_5(bidirectional_shift_register_63_out_5), .out_6(bidirectional_shift_register_63_out_6),
    .out_7(bidirectional_shift_register_63_out_7), .out_8(bidirectional_shift_register_63_out_8));  // open: out_9
  Bidirectional_Shift_Register bidirectional_shift_register_64 (
    .in_1(bidirectional_shift_register_34_out_5), .in_2(bidirectional_shift_register_34_out_6),
    .in_3(bidirectional_shift_register_34_out_7), .in_4(bidirectional_shift_register_34_out_8),
    .out_5(bidirectional_shift_register_64_out_5), .out_6(bidirectional_shift_register_64_out_6),
    .out_7(bidirectional_shift_register_64_out_7), .out_8(bidirectional_shift_register_64_out_8));  // open: out_9
  Bidirectional_Shift_Register bidirectional_shift_register_65 (
    .in_1(bidirectional_shift_register_63_out_5), .in_2(bidirectional_shift_register_63_out_6),
    .in_3(bidirectional_shift_register_63_out_7), .in_4(bidirectional_shift_register_63_out_8),
    .out_5(bidirectional_shift_register_65_out_5), .out_6(bidirectional_shift_register_65_out_6),
    .out_7(bidirectional_shift_register_65_out_7), .out_8(bidirectional_shift_register_65_out_8));  // open: out_9
  Bidirectional_Shift_Register bidirectional_shift_register_66 (
    .in_1(bidirectional_shift_register_67_out_5), .in_2(bidirectional_shift_register_67_out_6),
    .in_3(bidirectional_shift_register_67_out_7), .in_4(bidirectional_shift_register_67_out_8),
    .out_5(bidirectional_shift_register_66_out_5), .out_6(bidirectional_shift_register_66_out_6),
    .out_7(bidirectional_shift_register_66_out_7), .out_8(bidirectional_shift_register_66_out_8));  // open: out_9
  Bidirectional_Shift_Register bidirectional_shift_register_67 (
    .in_1(bidirectional_shift_register_68_out_5), .in_2(bidirectional_shift_register_68_out_6),
    .in_3(bidirectional_shift_register_68_out_7), .in_4(bidirectional_shift_register_68_out_8),
    .out_5(bidirectional_shift_register_67_out_5), .out_6(bidirectional_shift_register_67_out_6),
    .out_7(bidirectional_shift_register_67_out_7), .out_8(bidirectional_shift_register_67_out_8));  // open: out_9
  Bidirectional_Shift_Register bidirectional_shift_register_68 (
    .in_1(bidirectional_shift_register_35_out_5), .in_2(bidirectional_shift_register_35_out_6),
    .in_3(bidirectional_shift_register_35_out_7), .in_4(bidirectional_shift_register_35_out_8),
    .out_5(bidirectional_shift_register_68_out_5), .out_6(bidirectional_shift_register_68_out_6),
    .out_7(bidirectional_shift_register_68_out_7), .out_8(bidirectional_shift_register_68_out_8));  // open: out_9
  Bidirectional_Shift_Register bidirectional_shift_register_69 (
    .in_1(bidirectional_shift_register_70_out_5), .in_2(bidirectional_shift_register_70_out_6),
    .in_3(bidirectional_shift_register_70_out_7), .in_4(bidirectional_shift_register_70_out_8),
    .out_5(bidirectional_shift_register_69_out_5), .out_6(bidirectional_shift_register_69_out_6),
    .out_7(bidirectional_shift_register_69_out_7), .out_8(bidirectional_shift_register_69_out_8));  // open: out_9
  Bidirectional_Shift_Register bidirectional_shift_register_70 (
    .in_1(bidirectional_shift_register_38_out_5), .in_2(bidirectional_shift_register_38_out_6),
    .in_3(bidirectional_shift_register_38_out_7), .in_4(bidirectional_shift_register_38_out_8),
    .out_5(bidirectional_shift_register_70_out_5), .out_6(bidirectional_shift_register_70_out_6),
    .out_7(bidirectional_shift_register_70_out_7), .out_8(bidirectional_shift_register_70_out_8));  // open: out_9
  Bidirectional_Shift_Register bidirectional_shift_register_71 (
    .in_1(bidirectional_shift_register_69_out_5), .in_2(bidirectional_shift_register_69_out_6),
    .in_3(bidirectional_shift_register_69_out_7), .in_4(bidirectional_shift_register_69_out_8),
    .out_5(bidirectional_shift_register_71_out_5), .out_6(bidirectional_shift_register_71_out_6),
    .out_7(bidirectional_shift_register_71_out_7), .out_8(bidirectional_shift_register_71_out_8));  // open: out_9
  Bidirectional_Shift_Register bidirectional_shift_register_72 (
    .in_1(bidirectional_shift_register_73_out_5), .in_2(bidirectional_shift_register_73_out_6),
    .in_3(bidirectional_shift_register_73_out_7), .in_4(bidirectional_shift_register_73_out_8),
    .out_5(bidirectional_shift_register_72_out_5), .out_6(bidirectional_shift_register_72_out_6),
    .out_7(bidirectional_shift_register_72_out_7), .out_8(bidirectional_shift_register_72_out_8));  // open: out_9
  Bidirectional_Shift_Register bidirectional_shift_register_73 (
    .in_1(bidirectional_shift_register_40_out_5), .in_2(bidirectional_shift_register_40_out_6),
    .in_3(bidirectional_shift_register_40_out_7), .in_4(bidirectional_shift_register_40_out_8),
    .out_5(bidirectional_shift_register_73_out_5), .out_6(bidirectional_shift_register_73_out_6),
    .out_7(bidirectional_shift_register_73_out_7), .out_8(bidirectional_shift_register_73_out_8));  // open: out_9
  Bidirectional_Shift_Register bidirectional_shift_register_74 (
    .in_1(bidirectional_shift_register_72_out_5), .in_2(bidirectional_shift_register_72_out_6),
    .in_3(bidirectional_shift_register_72_out_7), .in_4(bidirectional_shift_register_72_out_8),
    .out_5(bidirectional_shift_register_74_out_5), .out_6(bidirectional_shift_register_74_out_6),
    .out_7(bidirectional_shift_register_74_out_7), .out_8(bidirectional_shift_register_74_out_8));  // open: out_9
  Bidirectional_Shift_Register bidirectional_shift_register_75 (
    .in_1(bidirectional_shift_register_41_out_5), .in_2(bidirectional_shift_register_41_out_6),
    .in_3(bidirectional_shift_register_41_out_7), .in_4(bidirectional_shift_register_41_out_8),
    .out_5(bidirectional_shift_register_75_out_5), .out_6(bidirectional_shift_register_75_out_6),
    .out_7(bidirectional_shift_register_75_out_7), .out_8(bidirectional_shift_register_75_out_8));  // open: out_9
  Bidirectional_Shift_Register bidirectional_shift_register_76 (
    .in_1(bidirectional_shift_register_77_out_5), .in_2(bidirectional_shift_register_77_out_6),
    .in_3(bidirectional_shift_register_77_out_7), .in_4(bidirectional_shift_register_77_out_8),
    .out_5(bidirectional_shift_register_76_out_5), .out_6(bidirectional_shift_register_76_out_6),
    .out_7(bidirectional_shift_register_76_out_7), .out_8(bidirectional_shift_register_76_out_8));  // open: out_9
  Bidirectional_Shift_Register bidirectional_shift_register_77 (
    .in_1(bidirectional_shift_register_75_out_5), .in_2(bidirectional_shift_register_75_out_6),
    .in_3(bidirectional_shift_register_75_out_7), .in_4(bidirectional_shift_register_75_out_8),
    .out_5(bidirectional_shift_register_77_out_5), .out_6(bidirectional_shift_register_77_out_6),
    .out_7(bidirectional_shift_register_77_out_7), .out_8(bidirectional_shift_register_77_out_8));  // open: out_9
  Bidirectional_Shift_Register bidirectional_shift_register_78 (
    .in_1(bidirectional_shift_register_79_out_5), .in_2(bidirectional_shift_register_79_out_6),
    .in_3(bidirectional_shift_register_79_out_7), .in_4(bidirectional_shift_register_79_out_8),
    .out_5(bidirectional_shift_register_78_out_5), .out_6(bidirectional_shift_register_78_out_6),
    .out_7(bidirectional_shift_register_78_out_7), .out_8(bidirectional_shift_register_78_out_8));  // open: out_9
  Bidirectional_Shift_Register bidirectional_shift_register_79 (
    .in_1(bidirectional_shift_register_80_out_5), .in_2(bidirectional_shift_register_80_out_6),
    .in_3(bidirectional_shift_register_80_out_7), .in_4(bidirectional_shift_register_80_out_8),
    .out_5(bidirectional_shift_register_79_out_5), .out_6(bidirectional_shift_register_79_out_6),
    .out_7(bidirectional_shift_register_79_out_7), .out_8(bidirectional_shift_register_79_out_8));  // open: out_9
  Bidirectional_Shift_Register bidirectional_shift_register_80 (
    .in_1(bidirectional_shift_register_44_out_5), .in_2(bidirectional_shift_register_44_out_6),
    .in_3(bidirectional_shift_register_44_out_7), .in_4(bidirectional_shift_register_44_out_8),
    .out_5(bidirectional_shift_register_80_out_5), .out_6(bidirectional_shift_register_80_out_6),
    .out_7(bidirectional_shift_register_80_out_7), .out_8(bidirectional_shift_register_80_out_8));  // open: out_9
  Bidirectional_Shift_Register bidirectional_shift_register_81 (
    .in_1(bidirectional_shift_register_82_out_5), .in_2(bidirectional_shift_register_82_out_6),
    .in_3(bidirectional_shift_register_82_out_7), .in_4(bidirectional_shift_register_82_out_8),
    .out_5(bidirectional_shift_register_81_out_5), .out_6(bidirectional_shift_register_81_out_6),
    .out_7(bidirectional_shift_register_81_out_7), .out_8(bidirectional_shift_register_81_out_8));  // open: out_9
  Bidirectional_Shift_Register bidirectional_shift_register_82 (
    .in_1(bidirectional_shift_register_83_out_5), .in_2(bidirectional_shift_register_83_out_6),
    .in_3(bidirectional_shift_register_83_out_7), .in_4(bidirectional_shift_register_83_out_8),
    .out_5(bidirectional_shift_register_82_out_5), .out_6(bidirectional_shift_register_82_out_6),
    .out_7(bidirectional_shift_register_82_out_7), .out_8(bidirectional_shift_register_82_out_8));  // open: out_9
  Bidirectional_Shift_Register bidirectional_shift_register_83 (
    .in_1(bidirectional_shift_register_46_out_5), .in_2(bidirectional_shift_register_46_out_6),
    .in_3(bidirectional_shift_register_46_out_7), .in_4(bidirectional_shift_register_46_out_8),
    .out_5(bidirectional_shift_register_83_out_5), .out_6(bidirectional_shift_register_83_out_6),
    .out_7(bidirectional_shift_register_83_out_7), .out_8(bidirectional_shift_register_83_out_8));  // open: out_9
  Bidirectional_Shift_Register bidirectional_shift_register_84 (
    .in_1(bidirectional_shift_register_86_out_5), .in_2(bidirectional_shift_register_86_out_6),
    .in_3(bidirectional_shift_register_86_out_7), .in_4(bidirectional_shift_register_86_out_8),
    .out_5(bidirectional_shift_register_84_out_5), .out_6(bidirectional_shift_register_84_out_6),
    .out_7(bidirectional_shift_register_84_out_7), .out_8(bidirectional_shift_register_84_out_8));  // open: out_9
  Bidirectional_Shift_Register bidirectional_shift_register_85 (
    .in_1(bidirectional_shift_register_84_out_5), .in_2(bidirectional_shift_register_84_out_6),
    .in_3(bidirectional_shift_register_84_out_7), .in_4(bidirectional_shift_register_84_out_8),
    .out_5(bidirectional_shift_register_85_out_5), .out_6(bidirectional_shift_register_85_out_6),
    .out_7(bidirectional_shift_register_85_out_7), .out_8(bidirectional_shift_register_85_out_8));  // open: out_9
  Bidirectional_Shift_Register bidirectional_shift_register_86 (
    .in_1(bidirectional_shift_register_48_out_5), .in_2(bidirectional_shift_register_48_out_6),
    .in_3(bidirectional_shift_register_48_out_7), .in_4(bidirectional_shift_register_48_out_8),
    .out_5(bidirectional_shift_register_86_out_5), .out_6(bidirectional_shift_register_86_out_6),
    .out_7(bidirectional_shift_register_86_out_7), .out_8(bidirectional_shift_register_86_out_8));  // open: out_9
  Bidirectional_Shift_Register bidirectional_shift_register_87 (
    .in_1(bidirectional_shift_register_49_out_5), .in_2(bidirectional_shift_register_49_out_6),
    .in_3(bidirectional_shift_register_49_out_7), .in_4(bidirectional_shift_register_49_out_8),
    .out_5(bidirectional_shift_register_87_out_5), .out_6(bidirectional_shift_register_87_out_6),
    .out_7(bidirectional_shift_register_87_out_7), .out_8(bidirectional_shift_register_87_out_8));  // open: out_9
  Bidirectional_Shift_Register bidirectional_shift_register_88 (
    .in_1(bidirectional_shift_register_87_out_5), .in_2(bidirectional_shift_register_87_out_6),
    .in_3(bidirectional_shift_register_87_out_7), .in_4(bidirectional_shift_register_87_out_8),
    .out_5(bidirectional_shift_register_88_out_5), .out_6(bidirectional_shift_register_88_out_6),
    .out_7(bidirectional_shift_register_88_out_7), .out_8(bidirectional_shift_register_88_out_8));  // open: out_9
  Bidirectional_Shift_Register bidirectional_shift_register_89 (
    .in_1(bidirectional_shift_register_88_out_5), .in_2(bidirectional_shift_register_88_out_6),
    .in_3(bidirectional_shift_register_88_out_7), .in_4(bidirectional_shift_register_88_out_8),
    .out_5(bidirectional_shift_register_89_out_5), .out_6(bidirectional_shift_register_89_out_6),
    .out_7(bidirectional_shift_register_89_out_7), .out_8(bidirectional_shift_register_89_out_8));  // open: out_9
  Bidirectional_Shift_Register bidirectional_shift_register_90 (
    .in_1(bidirectional_shift_register_91_out_5), .in_2(bidirectional_shift_register_91_out_6),
    .in_3(bidirectional_shift_register_91_out_7), .in_4(bidirectional_shift_register_91_out_8),
    .out_5(bidirectional_shift_register_90_out_5), .out_6(bidirectional_shift_register_90_out_6),
    .out_7(bidirectional_shift_register_90_out_7), .out_8(bidirectional_shift_register_90_out_8));  // open: out_9
  Bidirectional_Shift_Register bidirectional_shift_register_91 (
    .in_1(bidirectional_shift_register_92_out_5), .in_2(bidirectional_shift_register_92_out_6),
    .in_3(bidirectional_shift_register_92_out_7), .in_4(bidirectional_shift_register_92_out_8),
    .out_5(bidirectional_shift_register_91_out_5), .out_6(bidirectional_shift_register_91_out_6),
    .out_7(bidirectional_shift_register_91_out_7), .out_8(bidirectional_shift_register_91_out_8));  // open: out_9
  Bidirectional_Shift_Register bidirectional_shift_register_92 (
    .in_1(bidirectional_shift_register_51_out_5), .in_2(bidirectional_shift_register_51_out_6),
    .in_3(bidirectional_shift_register_51_out_7), .in_4(bidirectional_shift_register_51_out_8),
    .out_5(bidirectional_shift_register_92_out_5), .out_6(bidirectional_shift_register_92_out_6),
    .out_7(bidirectional_shift_register_92_out_7), .out_8(bidirectional_shift_register_92_out_8));  // open: out_9
  Bidirectional_Shift_Register bidirectional_shift_register_93 (
    .in_1(bidirectional_shift_register_94_out_5), .in_2(bidirectional_shift_register_94_out_6),
    .in_3(bidirectional_shift_register_94_out_7), .in_4(bidirectional_shift_register_94_out_8),
    .out_5(bidirectional_shift_register_93_out_5), .out_6(bidirectional_shift_register_93_out_6),
    .out_7(bidirectional_shift_register_93_out_7), .out_8(bidirectional_shift_register_93_out_8));  // open: out_9
  Bidirectional_Shift_Register bidirectional_shift_register_94 (
    .in_1(bidirectional_shift_register_54_out_5), .in_2(bidirectional_shift_register_54_out_6),
    .in_3(bidirectional_shift_register_54_out_7), .in_4(bidirectional_shift_register_54_out_8),
    .out_5(bidirectional_shift_register_94_out_5), .out_6(bidirectional_shift_register_94_out_6),
    .out_7(bidirectional_shift_register_94_out_7), .out_8(bidirectional_shift_register_94_out_8));  // open: out_9
  Bidirectional_Shift_Register bidirectional_shift_register_95 (
    .in_1(bidirectional_shift_register_93_out_5), .in_2(bidirectional_shift_register_93_out_6),
    .in_3(bidirectional_shift_register_93_out_7), .in_4(bidirectional_shift_register_93_out_8),
    .out_5(bidirectional_shift_register_95_out_5), .out_6(bidirectional_shift_register_95_out_6),
    .out_7(bidirectional_shift_register_95_out_7), .out_8(bidirectional_shift_register_95_out_8));  // open: out_9
  Bidirectional_Shift_Register bidirectional_shift_register_96 (
    .in_1(bidirectional_shift_register_56_out_5), .in_2(bidirectional_shift_register_56_out_6),
    .in_3(bidirectional_shift_register_56_out_7), .in_4(bidirectional_shift_register_56_out_8),
    .out_5(bidirectional_shift_register_96_out_5), .out_6(bidirectional_shift_register_96_out_6),
    .out_7(bidirectional_shift_register_96_out_7), .out_8(bidirectional_shift_register_96_out_8));  // open: out_9
  Bidirectional_Shift_Register bidirectional_shift_register_97 (
    .in_1(bidirectional_shift_register_96_out_5), .in_2(bidirectional_shift_register_96_out_6),
    .in_3(bidirectional_shift_register_96_out_7), .in_4(bidirectional_shift_register_96_out_8),
    .out_5(bidirectional_shift_register_97_out_5), .out_6(bidirectional_shift_register_97_out_6),
    .out_7(bidirectional_shift_register_97_out_7), .out_8(bidirectional_shift_register_97_out_8));  // open: out_9
  Bidirectional_Shift_Register bidirectional_shift_register_98 (
    .in_1(bidirectional_shift_register_97_out_5), .in_2(bidirectional_shift_register_97_out_6),
    .in_3(bidirectional_shift_register_97_out_7), .in_4(bidirectional_shift_register_97_out_8),
    .out_5(bidirectional_shift_register_98_out_5), .out_6(bidirectional_shift_register_98_out_6),
    .out_7(bidirectional_shift_register_98_out_7), .out_8(bidirectional_shift_register_98_out_8));  // open: out_9
  Bidirectional_Shift_Register bidirectional_shift_register_99 (
    .in_1(bidirectional_shift_register_58_out_5), .in_2(bidirectional_shift_register_58_out_6),
    .in_3(bidirectional_shift_register_58_out_7), .in_4(bidirectional_shift_register_58_out_8),
    .out_6(out_5[0]));  // open: out_5, out_7, out_9, out_8
  Bidirectional_Shift_Register bidirectional_shift_register_100 (
    .in_1(bidirectional_shift_register_62_out_5), .in_2(bidirectional_shift_register_62_out_6),
    .in_3(bidirectional_shift_register_62_out_7), .in_4(bidirectional_shift_register_62_out_8),
    .out_6(out_5[1]));  // open: out_5, out_7, out_9, out_8
  Bidirectional_Shift_Register bidirectional_shift_register_101 (
    .in_1(bidirectional_shift_register_65_out_5), .in_2(bidirectional_shift_register_65_out_6),
    .in_3(bidirectional_shift_register_65_out_7), .in_4(bidirectional_shift_register_65_out_8),
    .out_6(out_5[2]));  // open: out_5, out_7, out_9, out_8
  Bidirectional_Shift_Register bidirectional_shift_register_102 (
    .in_1(bidirectional_shift_register_66_out_5), .in_2(bidirectional_shift_register_66_out_6),
    .in_3(bidirectional_shift_register_66_out_7), .in_4(bidirectional_shift_register_66_out_8),
    .out_6(out_5[3]));  // open: out_5, out_7, out_9, out_8
  Bidirectional_Shift_Register bidirectional_shift_register_103 (
    .in_1(bidirectional_shift_register_71_out_5), .in_2(bidirectional_shift_register_71_out_6),
    .in_3(bidirectional_shift_register_71_out_7), .in_4(bidirectional_shift_register_71_out_8),
    .out_6(out_5[4]));  // open: out_5, out_7, out_9, out_8
  Bidirectional_Shift_Register bidirectional_shift_register_104 (
    .in_1(bidirectional_shift_register_74_out_5), .in_2(bidirectional_shift_register_74_out_6),
    .in_3(bidirectional_shift_register_74_out_7), .in_4(bidirectional_shift_register_74_out_8),
    .out_6(out_5[5]));  // open: out_5, out_7, out_9, out_8
  Bidirectional_Shift_Register bidirectional_shift_register_105 (
    .in_1(bidirectional_shift_register_76_out_5), .in_2(bidirectional_shift_register_76_out_6),
    .in_3(bidirectional_shift_register_76_out_7), .in_4(bidirectional_shift_register_76_out_8),
    .out_6(out_5[6]));  // open: out_5, out_7, out_9, out_8
  Bidirectional_Shift_Register bidirectional_shift_register_106 (
    .in_1(bidirectional_shift_register_78_out_5), .in_2(bidirectional_shift_register_78_out_6),
    .in_3(bidirectional_shift_register_78_out_7), .in_4(bidirectional_shift_register_78_out_8),
    .out_6(out_5[7]));  // open: out_5, out_7, out_9, out_8
  Bidirectional_Shift_Register bidirectional_shift_register_107 (
    .in_1(bidirectional_shift_register_81_out_5), .in_2(bidirectional_shift_register_81_out_6),
    .in_3(bidirectional_shift_register_81_out_7), .in_4(bidirectional_shift_register_81_out_8),
    .out_6(out_5[8]));  // open: out_5, out_7, out_9, out_8
  Bidirectional_Shift_Register bidirectional_shift_register_108 (
    .in_1(bidirectional_shift_register_85_out_5), .in_2(bidirectional_shift_register_85_out_6),
    .in_3(bidirectional_shift_register_85_out_7), .in_4(bidirectional_shift_register_85_out_8),
    .out_6(out_5[9]));  // open: out_5, out_7, out_9, out_8
  Bidirectional_Shift_Register bidirectional_shift_register_109 (
    .in_1(bidirectional_shift_register_89_out_5), .in_2(bidirectional_shift_register_89_out_6),
    .in_3(bidirectional_shift_register_89_out_7), .in_4(bidirectional_shift_register_89_out_8),
    .out_6(out_5[10]));  // open: out_5, out_7, out_9, out_8
  Bidirectional_Shift_Register bidirectional_shift_register_110 (
    .in_1(bidirectional_shift_register_90_out_5), .in_2(bidirectional_shift_register_90_out_6),
    .in_3(bidirectional_shift_register_90_out_7), .in_4(bidirectional_shift_register_90_out_8),
    .out_6(out_5[11]));  // open: out_5, out_7, out_9, out_8
  Bidirectional_Shift_Register bidirectional_shift_register_111 (
    .in_1(bidirectional_shift_register_95_out_5), .in_2(bidirectional_shift_register_95_out_6),
    .in_3(bidirectional_shift_register_95_out_7), .in_4(bidirectional_shift_register_95_out_8),
    .out_6(out_5[12]));  // open: out_5, out_7, out_9, out_8
  Bidirectional_Shift_Register bidirectional_shift_register_112 (
    .in_1(bidirectional_shift_register_98_out_5), .in_2(bidirectional_shift_register_98_out_6),
    .in_3(bidirectional_shift_register_98_out_7), .in_4(bidirectional_shift_register_98_out_8),
    .out_6(out_5[13]));  // open: out_5, out_7, out_9, out_8
endmodule
